# Fritzing sketch ButtonSchematic (saved by Fritzing 0.8.0b)
breadboards: 1

parts:
  Part1 = Arduino Uno (Rev3)
  R1 = Resistor [tolerance=±5% resistance=220 package=THT]
  LED1 = LED - 5mm [color="Red (633nm)" package="5 mm [THT]"]
  S1 = Pushbutton [package=THT]

nets (from the schematic view):
  N1: Part1.ICSP_SCK, Part1.D13/SCK, R1.Pin_0
  N2: Part1.GND, LED1.cathode, S1.leg1
  N3: Part1.D8, S1.leg0
  N4: R1.Pin_1, LED1.anode
