# Fritzing sketch ButtonSchematicAnalog (saved by Fritzing 0.8.0b)
breadboards: 1

parts:
  Part1 = Arduino Uno (Rev3)
  R1 = Resistor [tolerance=±5% resistance=220 package=THT]
  S1 = Pushbutton [package=THT]
  LED1 = LED - 5mm [color="Red (633nm)" package="5 mm [THT]"]

nets:
  N1: Part1.GND, LED1.cathode
  N2: Part1.3V3, R1.Pin_0
  N3: R1.Pin_1, S1.leg1
  N4: S1.leg0, LED1.anode
