# Fritzing sketch Analog_LED_Pulsing (saved by Fritzing 0.8.0b)
breadboards: 1

parts:
  Part1 = Arduino Uno (Rev3)
  R1 = Resistor [tolerance=±5% resistance=220 package=THT]
  LED1 = LED - 5mm [color="Red (633nm)" package="5 mm [THT]"]

nets:
  N1: Part1.GND, R1.Pin_0
  N2: Part1.D9_PWM, LED1.anode
  N3: R1.Pin_1, LED1.cathode
