# Fritzing sketch Analog-LED-RGB (saved by Fritzing 0.8.0b)
breadboards: 1

parts:
  Part1 = Arduino Uno (Rev3)
  R1 = Resistor [tolerance=±5% resistance=220 package=THT]
  R2 = Resistor [tolerance=±5% resistance=220 package=THT]
  R3 = Resistor [tolerance=±5% resistance=220 package=THT]
  LED1 = RGB LED (com. anode, rbg) [package="5 mm [THT]"]

nets:
  N1: Part1.GND, R1.Pin_0, R2.Pin_0, R3.Pin_0
  N2: Part1.D9_PWM, LED1.common_anode
  N3: R1.Pin_1, LED1.red_cathode
  N4: R2.Pin_1, LED1.blue_cathode
  N5: R3.Pin_1, LED1.green_cathode
