# Fritzing sketch tonePitchFollower (saved by Fritzing 0.8.0b)
breadboards: 1

parts:
  Part1 = Arduino Uno (Rev3)
  R1 = Resistor [tolerance=±5% resistance=220 package=THT]
  J1 = Piezo Speaker
  R2 = Photocell (LDR) [package=THT]
  R3 = Resistor [tolerance=±5% resistance=220 package=THT]

nets:
  N1: Part1.A0, R2.pin_0, R3.Pin_1
  N2: Part1.GND, J1.pin1, R3.Pin_0
  N3: Part1.D9_PWM, R1.Pin_1
  N4: Part1.5V, R2.pin_1
  N5: R1.Pin_0, J1.pin2
