# Fritzing sketch KnobSchematic (saved by Fritzing 0.8.0b)
breadboards: 1

parts:
  R1 = Rotary Potentiometer (Small)
  R2 = Resistor [tolerance=±5% resistance=220 package=THT]
  LED1 = LED - 5mm [color="Red (633nm)" package="5 mm [THT]"]
  Part1 = Arduino Uno (Rev3)

nets:
  N1: R1.leg1, Part1.5V
  N2: R1.wiper, Part1.A5/SCL
  N3: R1.leg2, LED1.anode, Part1.GND
  N4: R2.Pin_0, Part1.ICSP_MOSI, Part1.D11_PWM/MOSI
  N5: R2.Pin_1, LED1.cathode
