# Fritzing sketch bleepagram (saved by Fritzing 0.8.0b)
breadboards: 1

parts:
  R1 = Rotary Potentiometer (Small)
  R2 = Rotary Potentiometer (Small)
  R3 = Rotary Potentiometer (Small)
  R4 = Rotary Potentiometer (Small)
  R5 = Rotary Potentiometer (Small)
  R6 = Rotary Potentiometer (Small)
  R7 = Rotary Potentiometer (Small)
  LED1 = LED - 5mm [color="Red (633nm)" package="5 mm [THT]"]
  LED2 = LED - 5mm [color="Red (633nm)" package="5 mm [THT]"]
  LED3 = LED - 5mm [color="Red (633nm)" package="5 mm [THT]"]
  LED4 = LED - 5mm [color="Red (633nm)" package="5 mm [THT]"]
  LED5 = LED - 5mm [color="Red (633nm)" package="5 mm [THT]"]
  J1 = Piezo Speaker
  Part1 = Arduino Uno (Rev3)
  R8 = Resistor [tolerance=±5% package=axial-0.3]  # not connected
  R8_2 = Resistor [tolerance=±5% package="2512 [SMD]"]  # not connected
  R9 = Resistor [tolerance=±5% resistance=220 package=THT]
  R10 = Resistor [tolerance=±5% resistance=220 package=THT]

nets:
  N1: R1.leg1, R2.leg1, R3.leg1, R4.leg1, R5.leg1, R6.leg1, R7.leg1, J1.pin1, Part1.GND, R9.Pin_1, R10.Pin_1
  N2: R1.wiper, Part1.A1
  N3: R1.leg2, R2.leg2, R3.leg2, R4.leg2, R5.leg2, R6.leg2, R7.leg2
  N4: R2.wiper, Part1.A2
  N5: R3.wiper, Part1.A3
  N6: R4.wiper, Part1.A4/SDA
  N7: R5.wiper, Part1.A5/SCL
  N8: R6.wiper, Part1.A0
  N9: R7.wiper, J1.pin2
  N10: LED1.cathode, Part1.D8
  N11: LED1.anode, LED2.anode, LED3.anode, LED4.anode, R9.Pin_0
  N12: LED2.cathode, Part1.D9_PWM
  N13: LED3.cathode, Part1.D10_PWM/SS
  N14: LED4.cathode, Part1.D11_PWM/MOSI
  N15: LED5.cathode, Part1.D12/MISO
  N16: LED5.anode, R10.Pin_0
